# Fritzing sketch PillPal-Hardware Diagram (saved by Fritzing 1.0.4)
breadboards: 1

parts:
  MCU1 = Raspberry Pi Zero
  LED1 = LED - 5mm [color="Red (633nm)" current=0.030A package="5 mm [THT]"]
  R1 = Resistor [tolerance=±5% resistance=220 package="0603 [SMD]"]
  Q1 = NPN-Transistor [package="TO92 [THT]"]
  Lilypad_Vibe1 = Lilypad Vibe Motor
  R2 = 1kΩ Resistor [package="1206 [SMD]"]
  U1 = LIPO-1000mAh [package=lipo-1000]
  D1 = Diode [package=diode-1n4001]
  S1 = Reed switch [package=THT]
  Q2 = NPN-Transistor [package="TO92 [THT]"]
  J1 = Piezo Speaker
  R3 = 1kΩ Resistor [package="1206 [SMD]"]
  C2 = Capacitor Polarized [package=cpol-radial-100uf-25v]
  C3 = Ceramic Capacitor [capacitance=100nF voltage=35V package="200 mil [THT, multilayer]"]
  Part1 = PowerBoost 500 Charger

nets:
  N1: MCU1.pin_2, MCU1.pin_4, Lilypad_Vibe1.Supply, D1.C, J1.pin2, C2.+, Part1.5.0V
  N2: MCU1.pin_6, MCU1.pin_9, MCU1.pin_14, MCU1.pin_34, LED1.cathode, Q1.E, U1.+, S1.pin_1, C2.-, C3.0, Part1.GND
  N3: MCU1.pin_8, S1.pin_2, C3.1
  N4: MCU1.pin_12, R1.Pin_1
  N5: MCU1.pin_32, R2.Pin_1
  N6: MCU1.pin_36, Q2.E
  N7: MCU1.pin_40, R3.Pin_1
  N8: LED1.anode, R1.Pin_0
  N9: Q1.B, R2.Pin_0
  N10: Q1.C, Lilypad_Vibe1.GND, D1.A
  N11: U1.-, Part1.VBAT_OUT
  N12: Q2.B, R3.Pin_0
  N13: Q2.C, J1.pin1

custom parts:
  1kΩ Resistor: A generic resistor
